# Fritzing sketch micap_device (saved by Fritzing 1.0.2b)
circuit board: 7.10407cm x 3.59393cm

parts:
  WeMos_D1_Mini1 = WeMos D1 Mini
  BAT_JST = Header 2 [package=jst-2-pth-ns]
  BMI160 = BMI160 breakout
  EXTRA_JST = Header 4 [package=jst-4-pth]
  D2 = Schottky Diode [part_number=1N5817 package="300 mil [THT]"]
  D1 = Schottky Diode [part_number=1N5817 package="300 mil [THT]"]
  S1 = SPST Switch [package=switch-spdt_kit]
  M_OUT = mystery part, 2 pins [chip_label=?]
  M_IN = mystery part, 2 pins [chip_label=?]
  TP1 = TP4056 [chip_label=TP4056 package="DIP (Dual Inline) [THT]"]
  R1 = Resistor [tolerance=±5% power=0.25W resistance=10k package=THT]
  R2 = Resistor [tolerance=±5% power=0.25W resistance=10k package=THT]

nets:
  N1: WeMos_D1_Mini1.3V3, BMI160.Pin_7, EXTRA_JST.2
  N2: WeMos_D1_Mini1.5V, D1.cathode
  N3: WeMos_D1_Mini1.A0, R1.Pin_1, R2.Pin_1
  N4: WeMos_D1_Mini1.D1, BMI160.Pin_9, EXTRA_JST.3
  N5: WeMos_D1_Mini1.D2, BMI160.Pin_10, EXTRA_JST.4
  N6: WeMos_D1_Mini1.G, BMI160.Pin_8, BMI160.Pin_12, EXTRA_JST.1, S1.O
  N7: BAT_JST.1, TP1.B-, R2.Pin_0
  N8: BAT_JST.2, TP1.B+, R1.Pin_0
  N9: D2.cathode, D1.anode, TP1.OUT+
  N10: D2.anode, M_OUT.pin1, M_IN.pin1, TP1.+
  N11: S1.P, TP1.OUT-
  N12: M_OUT.pin2, M_IN.pin2, TP1.-

custom parts:
  BMI160 breakout: BMI160 Latest Stance Accelerometer Gyroscope module 6 Dof inertial Measurement Sensors.
  TP4056: A DIP stand-in part for whatever IC you want. With 6 pins on a 300mil dual inline package (DIP) footprint.
